// Logisim project cpu.circ as structural Verilog
module IPdeco (
  input  OP1,
  input  OP2,
  input  OP3,
  input  OP4,
  input  OP5,
  input  OP6,
  input  FU1,
  input  FU2,
  input  FU3,
  input  FU4,
  input  FU5,
  input  FU6,
  output NOR,
  output ADD,
  output LW,
  output ADDI,
  output SW,
  output ADDIU,
  output BOE,
  output BNE,
  output ADDU,
  output SLT,
  output AND,
  output SLTI,
  output ANDI,
  output SLTU,
  output JMP,
  output SLL,
  output JAL,
  output SRA,
  output JR,
  output SRL,
  output SYSCALL,
  output SUB,
  output OR,
  output ORI
);

  wire not_1_out, not_2_out, not_3_out, not_4_out, not_5_out, not_6_out, not_7_out, not_8_out, not_9_out,
       not_10_out, not_11_out, not_12_out, not_13_out, not_14_out, not_15_out, not_16_out, not_17_out,
       not_18_out, not_19_out, not_20_out, not_21_out, not_22_out, not_23_out, not_24_out, not_25_out,
       not_26_out, not_27_out, not_28_out, not_29_out, not_30_out, not_31_out, not_32_out, not_33_out,
       not_34_out, not_35_out, not_36_out, not_37_out, not_38_out, not_39_out, not_40_out, not_41_out,
       not_42_out, not_43_out, not_44_out, not_45_out, not_46_out, not_47_out, not_48_out, not_49_out,
       not_50_out, not_51_out, not_52_out, not_53_out, not_54_out, not_55_out, not_56_out, not_57_out,
       not_58_out, not_59_out, not_60_out, not_61_out, not_62_out, not_63_out, not_64_out, not_65_out,
       not_66_out, not_67_out, not_68_out, not_69_out, not_70_out, not_71_out, not_72_out, not_73_out,
       not_74_out, not_75_out, not_76_out, not_77_out, not_78_out, not_79_out, not_80_out, not_81_out,
       not_82_out, not_83_out, not_84_out, not_85_out, not_86_out, not_87_out, not_88_out, not_89_out,
       not_90_out, not_91_out, not_92_out, not_93_out, not_94_out, not_95_out, not_96_out, not_97_out,
       not_98_out, not_99_out, not_100_out, not_101_out, not_102_out, not_103_out, not_104_out, not_105_out,
       not_106_out, not_107_out, not_108_out, not_109_out, not_110_out, not_111_out, not_112_out,
       not_113_out, not_114_out, not_115_out, not_116_out, not_117_out, not_118_out, not_119_out,
       not_120_out, not_121_out, not_122_out, not_123_out, not_124_out, not_125_out, not_126_out,
       not_127_out, not_128_out, not_129_out, not_130_out, not_131_out, not_132_out, not_133_out,
       not_134_out, not_135_out, not_136_out, not_137_out, not_138_out, not_139_out, not_140_out,
       not_141_out, not_142_out, not_143_out, not_144_out, not_145_out, not_146_out, not_147_out,
       not_148_out, not_149_out, not_150_out, not_151_out, not_152_out, not_153_out, not_154_out,
       not_155_out, not_156_out, not_157_out, not_158_out, not_159_out, not_160_out, not_161_out,
       not_162_out, not_163_out, not_164_out, not_165_out, not_166_out, not_167_out, not_168_out,
       not_169_out, not_170_out, not_171_out, not_172_out, not_173_out;

  not not_1 (not_1_out, OP1);
  not not_2 (not_2_out, OP2);
  not not_3 (not_3_out, OP3);
  not not_4 (not_4_out, OP4);
  not not_5 (not_5_out, OP5);
  not not_6 (not_6_out, OP6);
  not not_7 (not_7_out, FU2);
  not not_8 (not_8_out, FU3);
  not not_9 (not_9_out, OP2);
  not not_10 (not_10_out, OP3);
  not not_11 (not_11_out, OP4);
  not not_12 (not_12_out, OP2);
  not not_13 (not_13_out, OP4);
  not not_14 (not_14_out, OP1);
  not not_15 (not_15_out, OP2);
  not not_16 (not_16_out, OP3);
  not not_17 (not_17_out, OP5);
  not not_18 (not_18_out, OP6);
  not not_19 (not_19_out, OP1);
  not not_20 (not_20_out, OP2);
  not not_21 (not_21_out, OP3);
  not not_22 (not_22_out, OP5);
  not not_23 (not_23_out, OP1);
  not not_24 (not_24_out, OP2);
  not not_25 (not_25_out, OP3);
  not not_26 (not_26_out, OP4);
  not not_27 (not_27_out, OP5);
  not not_28 (not_28_out, OP6);
  not not_29 (not_29_out, FU2);
  not not_30 (not_30_out, FU4);
  not not_31 (not_31_out, FU6);
  not not_32 (not_32_out, OP1);
  not not_33 (not_33_out, OP2);
  not not_34 (not_34_out, OP4);
  not not_35 (not_35_out, OP6);
  not not_36 (not_36_out, OP1);
  not not_37 (not_37_out, OP2);
  not not_38 (not_38_out, OP3);
  not not_39 (not_39_out, OP4);
  not not_40 (not_40_out, OP5);
  not not_41 (not_41_out, OP6);
  not not_42 (not_42_out, FU2);
  not not_43 (not_43_out, FU4);
  not not_44 (not_44_out, OP1);
  not not_45 (not_45_out, OP2);
  not not_46 (not_46_out, OP3);
  not not_47 (not_47_out, OP4);
  not not_48 (not_48_out, OP6);
  not not_49 (not_49_out, OP1);
  not not_50 (not_50_out, OP2);
  not not_51 (not_51_out, OP3);
  not not_52 (not_52_out, OP4);
  not not_53 (not_53_out, OP6);
  not not_54 (not_54_out, OP1);
  not not_55 (not_55_out, OP2);
  not not_56 (not_56_out, OP3);
  not not_57 (not_57_out, OP4);
  not not_58 (not_58_out, OP5);
  not not_59 (not_59_out, OP6);
  not not_60 (not_60_out, FU1);
  not not_61 (not_61_out, FU2);
  not not_62 (not_62_out, FU4);
  not not_63 (not_63_out, FU5);
  not not_64 (not_64_out, FU6);
  not not_65 (not_65_out, OP1);
  not not_66 (not_66_out, OP2);
  not not_67 (not_67_out, OP3);
  not not_68 (not_68_out, OP4);
  not not_69 (not_69_out, OP5);
  not not_70 (not_70_out, OP6);
  not not_71 (not_71_out, FU1);
  not not_72 (not_72_out, FU2);
  not not_73 (not_73_out, FU5);
  not not_74 (not_74_out, FU6);
  and and_1 (NOR, not_1_out, not_2_out, not_3_out, not_4_out, not_5_out, not_6_out, FU1, not_7_out, not_8_out, FU4, FU5, FU6);
  and and_2 (LW, OP1, not_9_out, not_10_out, not_11_out, OP5, OP6);
  and and_3 (SW, OP1, not_12_out, OP3, not_13_out, OP5, OP6);
  and and_4 (BOE, not_14_out, not_15_out, not_16_out, OP4, not_17_out, not_18_out);
  and and_5 (BNE, not_19_out, not_20_out, not_21_out, OP4, not_22_out, OP6);
  and and_6 (SLT, not_23_out, not_24_out, not_25_out, not_26_out, not_27_out, not_28_out, FU1, not_29_out, FU3, not_30_out, FU5, not_31_out);
  and and_7 (SLTI, not_32_out, not_33_out, OP3, not_34_out, OP5, not_35_out);
  and and_8 (SLTU, not_36_out, not_37_out, not_38_out, not_39_out, not_40_out, not_41_out, FU1, not_42_out, FU3, not_43_out, FU5, FU6);
  and and_9 (JMP, not_44_out, not_45_out, not_46_out, not_47_out, OP5, not_48_out);
  and and_10 (JAL, not_49_out, not_50_out, not_51_out, not_52_out, OP5, not_53_out);
  and and_11 (JR, not_54_out, not_55_out, not_56_out, not_57_out, not_58_out, not_59_out, not_60_out, not_61_out, FU3, not_62_out, not_63_out, not_64_out);
  and and_12 (SYSCALL, not_65_out, not_66_out, not_67_out, not_68_out, not_69_out, not_70_out, not_71_out, not_72_out, FU3, FU4, not_73_out, not_74_out);
  not not_75 (not_75_out, OP1);
  not not_76 (not_76_out, OP2);
  not not_77 (not_77_out, OP3);
  not not_78 (not_78_out, OP4);
  not not_79 (not_79_out, OP5);
  not not_80 (not_80_out, OP6);
  not not_81 (not_81_out, FU2);
  not not_82 (not_82_out, FU3);
  not not_83 (not_83_out, FU4);
  not not_84 (not_84_out, FU5);
  not not_85 (not_85_out, FU6);
  not not_86 (not_86_out, OP1);
  not not_87 (not_87_out, OP2);
  not not_88 (not_88_out, OP4);
  not not_89 (not_89_out, OP5);
  not not_90 (not_90_out, OP6);
  not not_91 (not_91_out, OP1);
  not not_92 (not_92_out, OP2);
  not not_93 (not_93_out, OP4);
  not not_94 (not_94_out, OP5);
  not not_95 (not_95_out, OP1);
  not not_96 (not_96_out, OP2);
  not not_97 (not_97_out, OP3);
  not not_98 (not_98_out, OP4);
  not not_99 (not_99_out, OP5);
  not not_100 (not_100_out, OP6);
  not not_101 (not_101_out, FU2);
  not not_102 (not_102_out, FU3);
  not not_103 (not_103_out, FU4);
  not not_104 (not_104_out, FU5);
  not not_105 (not_105_out, OP1);
  not not_106 (not_106_out, OP2);
  not not_107 (not_107_out, OP3);
  not not_108 (not_108_out, OP4);
  not not_109 (not_109_out, OP5);
  not not_110 (not_110_out, OP6);
  not not_111 (not_111_out, FU2);
  not not_112 (not_112_out, FU3);
  not not_113 (not_113_out, FU5);
  not not_114 (not_114_out, FU6);
  not not_115 (not_115_out, OP1);
  not not_116 (not_116_out, OP2);
  not not_117 (not_117_out, OP5);
  not not_118 (not_118_out, OP6);
  not not_119 (not_119_out, OP1);
  not not_120 (not_120_out, OP2);
  not not_121 (not_121_out, OP3);
  not not_122 (not_122_out, OP4);
  not not_123 (not_123_out, OP5);
  not not_124 (not_124_out, OP6);
  not not_125 (not_125_out, FU1);
  not not_126 (not_126_out, FU2);
  not not_127 (not_127_out, FU3);
  not not_128 (not_128_out, FU4);
  not not_129 (not_129_out, FU5);
  not not_130 (not_130_out, FU6);
  not not_131 (not_131_out, OP1);
  not not_132 (not_132_out, OP2);
  not not_133 (not_133_out, OP3);
  not not_134 (not_134_out, OP4);
  not not_135 (not_135_out, OP5);
  not not_136 (not_136_out, OP6);
  not not_137 (not_137_out, FU1);
  not not_138 (not_138_out, FU2);
  not not_139 (not_139_out, FU3);
  not not_140 (not_140_out, FU4);
  not not_141 (not_141_out, OP1);
  not not_142 (not_142_out, OP2);
  not not_143 (not_143_out, OP3);
  not not_144 (not_144_out, OP4);
  not not_145 (not_145_out, OP5);
  not not_146 (not_146_out, OP6);
  not not_147 (not_147_out, FU1);
  not not_148 (not_148_out, FU2);
  not not_149 (not_149_out, FU3);
  not not_150 (not_150_out, FU4);
  not not_151 (not_151_out, FU6);
  not not_152 (not_152_out, OP1);
  not not_153 (not_153_out, OP2);
  not not_154 (not_154_out, OP3);
  not not_155 (not_155_out, OP4);
  not not_156 (not_156_out, OP5);
  not not_157 (not_157_out, OP6);
  not not_158 (not_158_out, FU2);
  not not_159 (not_159_out, FU3);
  not not_160 (not_160_out, FU4);
  not not_161 (not_161_out, FU6);
  not not_162 (not_162_out, OP1);
  not not_163 (not_163_out, OP2);
  not not_164 (not_164_out, OP3);
  not not_165 (not_165_out, OP4);
  not not_166 (not_166_out, OP5);
  not not_167 (not_167_out, OP6);
  not not_168 (not_168_out, FU2);
  not not_169 (not_169_out, FU3);
  not not_170 (not_170_out, FU5);
  not not_171 (not_171_out, OP1);
  not not_172 (not_172_out, OP2);
  not not_173 (not_173_out, OP5);
  and and_13 (ADDI, not_86_out, not_87_out, OP3, not_88_out, not_89_out, not_90_out);
  and and_14 (ADDIU, not_91_out, not_92_out, OP3, not_93_out, not_94_out, OP6);
  and and_15 (ANDI, not_115_out, not_116_out, OP3, OP4, not_117_out, not_118_out);
  and and_16 (ORI, not_171_out, not_172_out, OP3, OP4, not_173_out, OP6);
  and and_17 (ADD, not_75_out, not_76_out, not_77_out, not_78_out, not_79_out, not_80_out, FU1, not_81_out, not_82_out, not_83_out, not_84_out, not_85_out);
  and and_18 (ADDU, not_95_out, not_96_out, not_97_out, not_98_out, not_99_out, not_100_out, FU1, not_101_out, not_102_out, not_103_out, not_104_out, FU6);
  and and_19 (AND, not_105_out, not_106_out, not_107_out, not_108_out, not_109_out, not_110_out, FU1, not_111_out, not_112_out, FU4, not_113_out, not_114_out);
  and and_20 (SLL, not_119_out, not_120_out, not_121_out, not_122_out, not_123_out, not_124_out, not_125_out, not_126_out, not_127_out, not_128_out, not_129_out, not_130_out);
  and and_21 (SRA, not_131_out, not_132_out, not_133_out, not_134_out, not_135_out, not_136_out, not_137_out, not_138_out, not_139_out, not_140_out, FU5, FU6);
  and and_22 (SRL, not_141_out, not_142_out, not_143_out, not_144_out, not_145_out, not_146_out, not_147_out, not_148_out, not_149_out, not_150_out, FU5, not_151_out);
  and and_23 (SUB, not_152_out, not_153_out, not_154_out, not_155_out, not_156_out, not_157_out, FU1, not_158_out, not_159_out, not_160_out, FU5, not_161_out);
  and and_24 (OR, not_162_out, not_163_out, not_164_out, not_165_out, not_166_out, not_167_out, FU1, not_168_out, not_169_out, FU4, not_170_out, FU6);
endmodule

module CLU (
  input  [5:0] op,
  input  [5:0] fc,
  output MemtoReg,
  output MemWrite,
  output Branch,
  output ALUSrc,
  output RegDst,
  output RegWrite,
  output [3:0] ALUC
);

  wire ipdeco_1_add, ipdeco_1_addi, ipdeco_1_addiu, ipdeco_1_addu, ipdeco_1_and, ipdeco_1_andi, ipdeco_1_bne,
       ipdeco_1_boe, ipdeco_1_jal, ipdeco_1_jmp, ipdeco_1_jr, ipdeco_1_lw, ipdeco_1_nor, ipdeco_1_or,
       ipdeco_1_ori, ipdeco_1_sll, ipdeco_1_slt, ipdeco_1_slti, ipdeco_1_sltu, ipdeco_1_sra, ipdeco_1_srl,
       ipdeco_1_sub, ipdeco_1_sw, ipdeco_1_syscall;

  IPdeco ipdeco_1 (
    .OP1(op[5]), .OP2(op[4]), .OP3(op[3]), .OP4(op[2]), .OP5(op[1]), .OP6(op[0]), .FU1(fc[5]), .FU2(fc[4]),
    .FU3(fc[3]), .FU4(fc[2]), .FU5(fc[1]), .FU6(fc[0]), .NOR(ipdeco_1_nor), .ADD(ipdeco_1_add),
    .LW(ipdeco_1_lw), .ADDI(ipdeco_1_addi), .SW(ipdeco_1_sw), .ADDIU(ipdeco_1_addiu), .BOE(ipdeco_1_boe),
    .BNE(ipdeco_1_bne), .ADDU(ipdeco_1_addu), .SLT(ipdeco_1_slt), .AND(ipdeco_1_and), .SLTI(ipdeco_1_slti),
    .ANDI(ipdeco_1_andi), .SLTU(ipdeco_1_sltu), .JMP(ipdeco_1_jmp), .SLL(ipdeco_1_sll), .JAL(ipdeco_1_jal),
    .SRA(ipdeco_1_sra), .JR(ipdeco_1_jr), .SRL(ipdeco_1_srl), .SYSCALL(ipdeco_1_syscall), .SUB(ipdeco_1_sub),
    .OR(ipdeco_1_or), .ORI(ipdeco_1_ori));
  or or_1 (ALUC[3], ipdeco_1_sltu, ipdeco_1_or, ipdeco_1_ori, ipdeco_1_slti, ipdeco_1_slt, ipdeco_1_nor);
  or or_2 (ALUC[2], ipdeco_1_sw, ipdeco_1_sub, ipdeco_1_add, ipdeco_1_sltu, ipdeco_1_andi, ipdeco_1_and, ipdeco_1_addu, ipdeco_1_addiu, ipdeco_1_addi, ipdeco_1_lw);
  or or_3 (ALUC[1], ipdeco_1_srl, ipdeco_1_andi, ipdeco_1_slti, ipdeco_1_sub, ipdeco_1_nor, ipdeco_1_and, ipdeco_1_slt);
  or or_4 (ALUC[0], ipdeco_1_sw, ipdeco_1_sra, ipdeco_1_andi, ipdeco_1_slti, ipdeco_1_and, ipdeco_1_slt, ipdeco_1_addu, ipdeco_1_addiu, ipdeco_1_addi, ipdeco_1_add, ipdeco_1_lw);
  IPdeco ipdeco_2 (
    .LW(ipdeco_1_lw), .SW(ipdeco_1_sw));  // open: OP1, OP2, OP3, OP4, OP5, OP6, FU1, FU2, FU3, FU4, FU5, FU6, NOR, ADD, ADDI, ADDIU, BOE, BNE, ADDU, SLT, AND, SLTI, ANDI, SLTU, JMP, SLL, JAL, SRA, JR, SRL, SYSCALL, SUB, OR, ORI
endmodule
