// Logisim project regfile.circ as structural Verilog: 3 circuits, main circuit main
module main (
  input  [4:0] Reg1_num,
  input  [4:0] Reg2,
  input  [4:0] Write_Reg_num,
  input  [31:0] Din,
  input  Write_Enable,
  input  Clock,
  output [31:0] Reg1,
  output [31:0] s0_Value,
  output [31:0] s1_Value,
  output [31:0] s2_Value,
  output [31:0] ra_Value,
  output [31:0] Reg2_2
);

  wire demultiplexer_1_out1, demultiplexer_1_out2, demultiplexer_1_out3, demultiplexer_1_out4,
       demultiplexer_1_out5, demultiplexer_1_out6, demultiplexer_1_out7, demultiplexer_1_out8,
       demultiplexer_1_out9, demultiplexer_1_out10, demultiplexer_1_out11, demultiplexer_1_out12,
       demultiplexer_1_out13, demultiplexer_1_out14, demultiplexer_1_out15, demultiplexer_1_out16,
       demultiplexer_1_out17, demultiplexer_1_out18, demultiplexer_1_out19, demultiplexer_1_out20,
       demultiplexer_1_out21, demultiplexer_1_out22, demultiplexer_1_out23, demultiplexer_1_out24,
       demultiplexer_1_out25, demultiplexer_1_out26, demultiplexer_1_out27, demultiplexer_1_out28,
       demultiplexer_1_out29, demultiplexer_1_out30, demultiplexer_1_out31;
  wire [31:0] register_1_q, register_2_q, register_4_q, register_5_q, register_6_q, register_8_q,
       register_9_q, register_10_q, register_12_q, register_13_q, register_14_q, register_15_q,
       register_16_q, register_17_q, register_18_q, register_19_q, register_20_q, register_21_q,
       register_22_q, register_23_q, register_25_q, register_26_q, register_27_q, register_28_q,
       register_29_q, register_30_q, register_31_q, register_32_q, sp;

  Demultiplexer #(.select(5), .enable("false")) demultiplexer_1 (
    .out1(demultiplexer_1_out1), .out2(demultiplexer_1_out2), .out3(demultiplexer_1_out3),
    .out4(demultiplexer_1_out4), .out5(demultiplexer_1_out5), .out6(demultiplexer_1_out6),
    .out7(demultiplexer_1_out7), .out8(demultiplexer_1_out8), .out9(demultiplexer_1_out9),
    .out10(demultiplexer_1_out10), .out11(demultiplexer_1_out11), .out12(demultiplexer_1_out12),
    .out13(demultiplexer_1_out13), .out14(demultiplexer_1_out14), .out15(demultiplexer_1_out15),
    .out16(demultiplexer_1_out16), .out17(demultiplexer_1_out17), .out18(demultiplexer_1_out18),
    .out19(demultiplexer_1_out19), .out20(demultiplexer_1_out20), .out21(demultiplexer_1_out21),
    .out22(demultiplexer_1_out22), .out23(demultiplexer_1_out23), .out24(demultiplexer_1_out24),
    .out25(demultiplexer_1_out25), .out26(demultiplexer_1_out26), .out27(demultiplexer_1_out27),
    .out28(demultiplexer_1_out28), .out29(demultiplexer_1_out29), .out30(demultiplexer_1_out30),
    .out31(demultiplexer_1_out31), .in(Write_Enable), .sel(Write_Reg_num));  // open: out0
  Register #(.width(32)) register_1 (.D({32{1'b0}}), .en(1'b1), .Q(register_1_q), .clk(1'b1), .clr(1'b0));
  Register #(.width(32)) register_2 (.D(Din), .en(demultiplexer_1_out8), .Q(register_2_q), .clk(Clock), .clr(1'b0));
  Register #(.width(32)) register_3 (.D(Din), .en(demultiplexer_1_out16), .Q(s0_Value), .clk(Clock), .clr(1'b0));
  Register #(.width(32)) register_4 (.D(Din), .en(demultiplexer_1_out24), .Q(register_4_q), .clk(Clock), .clr(1'b0));
  Register #(.width(32)) register_5 (.D(Din), .en(demultiplexer_1_out1), .Q(register_5_q), .clk(Clock), .clr(1'b0));
  Register #(.width(32)) register_6 (.D(Din), .en(demultiplexer_1_out9), .Q(register_6_q), .clk(Clock), .clr(1'b0));
  Register #(.width(32)) register_7 (.D(Din), .en(demultiplexer_1_out17), .Q(s1_Value), .clk(Clock), .clr(1'b0));
  Register #(.width(32)) register_8 (.D(Din), .en(demultiplexer_1_out25), .Q(register_8_q), .clk(Clock), .clr(1'b0));
  Register #(.width(32)) register_9 (.D(Din), .en(demultiplexer_1_out2), .Q(register_9_q), .clk(Clock), .clr(1'b0));
  Register #(.width(32)) register_10 (.D(Din), .en(demultiplexer_1_out10), .Q(register_10_q), .clk(Clock), .clr(1'b0));
  Register #(.width(32)) register_11 (.D(Din), .en(demultiplexer_1_out18), .Q(s2_Value), .clk(Clock), .clr(1'b0));
  Register #(.width(32)) register_12 (.D(Din), .en(demultiplexer_1_out26), .Q(register_12_q), .clk(Clock), .clr(1'b0));
  Register #(.width(32)) register_13 (.D(Din), .en(demultiplexer_1_out3), .Q(register_13_q), .clk(Clock), .clr(1'b0));
  Register #(.width(32)) register_14 (.D(Din), .en(demultiplexer_1_out11), .Q(register_14_q), .clk(Clock), .clr(1'b0));
  Register #(.width(32)) register_15 (.D(Din), .en(demultiplexer_1_out19), .Q(register_15_q), .clk(Clock), .clr(1'b0));
  Register #(.width(32)) register_16 (.D(Din), .en(demultiplexer_1_out27), .Q(register_16_q), .clk(Clock), .clr(1'b0));
  Register #(.width(32)) register_17 (.D(Din), .en(demultiplexer_1_out4), .Q(register_17_q), .clk(Clock), .clr(1'b0));
  Register #(.width(32)) register_18 (.D(Din), .en(demultiplexer_1_out12), .Q(register_18_q), .clk(Clock), .clr(1'b0));
  Register #(.width(32)) register_19 (.D(Din), .en(demultiplexer_1_out20), .Q(register_19_q), .clk(Clock), .clr(1'b0));
  Register #(.width(32)) register_20 (.D(Din), .en(demultiplexer_1_out28), .Q(register_20_q), .clk(Clock), .clr(1'b0));
  Register #(.width(32)) register_21 (.D(Din), .en(demultiplexer_1_out5), .Q(register_21_q), .clk(Clock), .clr(1'b0));
  Register #(.width(32)) register_22 (.D(Din), .en(demultiplexer_1_out13), .Q(register_22_q), .clk(Clock), .clr(1'b0));
  Register #(.width(32)) register_23 (.D(Din), .en(demultiplexer_1_out21), .Q(register_23_q), .clk(Clock), .clr(1'b0));
  Register #(.width(32)) register_24 (.D(Din), .en(demultiplexer_1_out29), .Q(sp), .clk(Clock), .clr(1'b0));
  Register #(.width(32)) register_25 (.D(Din), .en(demultiplexer_1_out6), .Q(register_25_q), .clk(Clock), .clr(1'b0));
  Register #(.width(32)) register_26 (.D(Din), .en(demultiplexer_1_out14), .Q(register_26_q), .clk(Clock), .clr(1'b0));
  Register #(.width(32)) register_27 (.D(Din), .en(demultiplexer_1_out22), .Q(register_27_q), .clk(Clock), .clr(1'b0));
  Register #(.width(32)) register_28 (.D(Din), .Q(register_28_q), .clk(Clock), .clr(1'b0));  // open: en
  Register #(.width(32)) register_29 (.D(Din), .en(demultiplexer_1_out7), .Q(register_29_q), .clk(Clock), .clr(1'b0));
  Register #(.width(32)) register_30 (.D(Din), .en(demultiplexer_1_out15), .Q(register_30_q), .clk(Clock), .clr(1'b0));
  Register #(.width(32)) register_31 (.D(Din), .en(demultiplexer_1_out23), .Q(register_31_q), .clk(Clock), .clr(1'b0));
  Register #(.width(32)) register_32 (.D(Din), .en(demultiplexer_1_out31), .Q(register_32_q), .clk(Clock), .clr(1'b0));
  Multiplexer #(.select(5), .width(32), .enable("false")) multiplexer_1 (
    .in0(register_1_q), .in1(register_5_q), .in2(register_9_q), .in3(register_13_q), .in4(register_17_q),
    .in5(register_21_q), .in6(register_25_q), .in7(register_29_q), .in8(register_2_q), .in9(register_6_q),
    .in10(register_10_q), .in11(register_14_q), .in12(register_18_q), .in13(register_22_q),
    .in14(register_26_q), .in15(register_30_q), .in16(s0_Value), .in17(s1_Value), .in18(s2_Value),
    .in19(register_15_q), .in20(register_19_q), .in21(register_23_q), .in22(register_27_q),
    .in23(register_31_q), .in24(register_4_q), .in25(register_8_q), .in26(register_12_q),
    .in27(register_16_q), .in28(register_20_q), .in29(sp), .in30(register_28_q), .in31(register_32_q),
    .out(Reg1), .sel(Reg1_num));
  Multiplexer #(.select(5), .width(32), .enable("false")) multiplexer_2 (
    .in0(register_1_q), .in1(register_5_q), .in2(register_9_q), .in3(register_13_q), .in4(register_17_q),
    .in5(register_21_q), .in6(register_25_q), .in7(register_29_q), .in8(register_2_q), .in9(register_6_q),
    .in10(register_10_q), .in11(register_14_q), .in12(register_18_q), .in13(register_22_q),
    .in14(register_26_q), .in15(register_30_q), .in16(s0_Value), .in17(s1_Value), .in18(s2_Value),
    .in19(register_15_q), .in20(register_19_q), .in21(register_23_q), .in22(register_27_q),
    .in23(register_31_q), .in24(register_4_q), .in25(register_8_q), .in26(register_12_q),
    .in27(register_16_q), .in28(register_20_q), .in29(sp), .in30(register_28_q), .in31(register_32_q),
    .out(Reg2_2), .sel(Reg2));

  // Other names for the same wires on the sheet: clk = Clock; ra[31:0] = ra_Value; reg2_num[4:0] = Reg2;
  //   reg2_t[31:0] = Reg2_2; s0[31:0] = s0_Value; s1[31:0] = s1_Value; s2[31:0] = s2_Value; WE = Write_Enable;
  //   write_data[31:0] = Din

  // Notes on the sheet:
  //   输入引脚
  //   输出引脚
  //   Debug引脚，便于观测寄存器值
  //   请勿修改引脚以及封装，直接使用隧道连接电路
endmodule

module test (
);

  main main_1 ();  // open: Reg1_num, Reg2, Write_Reg_num, Din, Write_Enable, Clock, Reg1, Reg2_2, s0_Value, s1_Value, s2_Value, ra_Value
endmodule

module RRAM (
);

  Counter #(.width(32), .max('hffffffff)) counter_1 ();  // open: load, D, count, Q, carry, clk, clr
  RAM #(.addrWidth(6), .dataWidth(32)) ram_1 ();  // open: addr, data, sel, clk, ld, clr
  main main_1 ();  // open: Reg1_num, Reg2, Write_Reg_num, Din, Write_Enable, Clock, Reg1, Reg2_2, s0_Value, s1_Value, s2_Value, ra_Value
  // ALU alu_1: pin names not known
endmodule
